// Logisim project projeto.circ as structural Verilog: 8 circuits, main circuit decoder
// DECODER
module decoder (
  input  A,
  input  B,
  input  C,
  input  C_2,
  output G,
  output F,
  output E,
  output D,
  output C_3,
  output B_2,
  output A_2,
  output H
);

  wire A_prime_C_out, A_prime_C_prime_out, AC_prime_out, and_1_out, and_2_out, and_3_out, and_4_out,
       and_5_out, and_6_out, and_7_out, and_8_out, and_9_out, and_10_out, and_11_out, and_12_out, and_13_out,
       and_14_out, and_16_out, BC_out, BD_out, C_D_out, not_1_out, not_2_out, not_3_out, not_4_out, or_1_out,
       or_2_out, or_3_out, or_4_out, or_5_out, or_6_out, or_7_out, or_8_out, or_9_out, or_10_out, or_11_out,
       or_14_out;

  not not_1 (not_1_out, A);
  not not_2 (not_2_out, B);
  not not_3 (not_3_out, C);
  not not_4 (not_4_out, C_2);
  and BC (BC_out, B, C);
  and A_prime_C_prime (A_prime_C_prime_out, not_1_out, not_3_out);
  or C_D (C_D_out, not_3_out, not_4_out);
  and A_prime_C (A_prime_C_out, not_1_out, C);
  and AC_prime (AC_prime_out, A, not_3_out);
  and BD (BD_out, B, C_2);
  or or_1 (or_1_out, A, B);
  and and_1 (and_1_out, not_2_out, not_3_out);
  and and_2 (and_2_out, C, or_1_out);
  and and_3 (and_3_out, not_3_out, not_4_out);
  and and_4 (and_4_out, not_1_out, C, C_2);
  or or_2 (or_2_out, and_1_out, BC_out);
  or or_3 (or_3_out, and_2_out, A_prime_C_prime_out);
  or or_4 (or_4_out, A, not_3_out);
  or or_5 (or_5_out, not_2_out, not_4_out);
  or or_6 (or_6_out, not_2_out, AC_prime_out);
  and and_5 (and_5_out, A, not_2_out);
  and and_6 (and_6_out, C_D_out, A);
  or or_7 (or_7_out, and_6_out, and_3_out);
  or or_8 (or_8_out, not_2_out, and_4_out);
  and and_7 (and_7_out, not_2_out, not_4_out);
  or or_9 (or_9_out, B, C);
  and and_8 (and_8_out, C, not_2_out, not_1_out);
  or or_10 (or_10_out, A, C_D_out);
  and and_9 (and_9_out, A, or_2_out);
  and and_10 (and_10_out, not_4_out, or_3_out);
  and and_11 (and_11_out, not_1_out, B, not_3_out);
  or or_11 (or_11_out, not_2_out, AC_prime_out, A_prime_C_out);
  and and_12 (and_12_out, or_4_out, BD_out);
  and and_13 (and_13_out, or_5_out, A_prime_C_out);
  and and_14 (and_14_out, not_4_out, or_6_out);
  or or_12 (B_2, or_7_out, or_8_out);
  or or_13 (A_2, A_prime_C_out, AC_prime_out, BD_out, and_7_out);
  and and_15 (H, A, or_9_out);
  or or_14 (or_14_out, AC_prime_out, and_8_out);
  and and_16 (and_16_out, B, or_10_out);
  and and_17 (E, not_4_out, or_11_out);
  or or_15 (D, and_12_out, and_13_out, and_14_out);
  or or_16 (C_3, C_2, and_5_out, BC_out, A_prime_C_prime_out);
  or u_G (G, or_14_out, and_16_out);
  or or_17 (F, and_9_out, and_10_out, and_11_out);
  _7_Segment_Display u_7_segment_display_1 (.b(H), .c(H));  // open: g, f, a, e, d, dp
  _7_Segment_Display u_7_segment_display_2 (.g(G), .f(F), .a(A_2), .b(B_2), .e(E), .d(D), .c(C_3));  // open: dp

  // Notes on the sheet:
  //   A
  //   C
  //   B
  //   F
  //   E
  //   D
endmodule

// Comp
module comparador (
  input  [4:0] A,
  input  [4:0] B,
  output out_3,
  output out_4,
  output out_5
);

  wire _0_out, _1_out, _2_out, _3_out, and_1_out, and_2_out, and_3_out, and_4_out, and_5_out, and_6_out,
       and_7_out, and_8_out, nor_1_out, nor_2_out, or_1_out, or_2_out, or_3_out, or_4_out, S_out, xor_1_out,
       xor_2_out;

  xor S (S_out, A[4], B[4]);
  xor _3 (_3_out, A[3], B[3]);
  xor _2 (_2_out, A[2], B[2]);
  xor _1 (_1_out, A[1], B[1]);
  xor _0 (_0_out, A[0], B[0]);
  and and_1 (and_1_out, A[4], B[4]);
  and and_2 (and_2_out, B[4], ~A[4]);  // AND_Gate
  xor xor_1 (xor_1_out, A[4], B[4]);
  xor xor_2 (xor_2_out, and_1_out, or_3_out);
  and and_3 (and_3_out, A[3], ~B[3]);  // AND_Gate
  and and_4 (and_4_out, ~_3_out, A[2], ~B[2]);  // AND_Gate
  and and_5 (and_5_out, ~_3_out, ~_2_out, A[1], ~B[1]);  // AND_Gate
  and and_6 (and_6_out, ~_3_out, ~_2_out, ~_1_out, A[0], ~B[0]);  // AND_Gate
  nor nor_1 (nor_1_out, S_out, _3_out, _2_out, _1_out, _0_out);
  or or_1 (or_1_out, A[3], A[2], A[1], A[0]);
  or or_2 (or_2_out, B[3], B[2], B[1], B[0]);
  and and_7 (and_7_out, and_2_out, xor_1_out);
  and and_8 (and_8_out, ~and_2_out, ~xor_1_out, xor_2_out);  // AND_Gate
  or or_3 (or_3_out, and_3_out, and_4_out, and_5_out, and_6_out);
  nor nor_2 (nor_2_out, or_1_out, or_2_out);
  or or_4 (or_4_out, and_7_out, and_8_out);
  or or_5 (out_3, nor_1_out, nor_2_out);
  xnor xnor_1 (out_5, out_3, out_4);
  and and_9 (out_4, ~nor_2_out, or_4_out);  // AND_Gate
endmodule

// mux
module mux1x1 (
  input  S2,
  input  S1,
  input  S0,
  input  A,
  input  B,
  input  C,
  output out_7
);

  wire and_1_out, and_2_out, and_3_out, not_1_out, not_2_out, not_3_out;

  not not_1 (not_1_out, S2);
  not not_2 (not_2_out, S1);
  not not_3 (not_3_out, S0);
  and and_1 (and_1_out, not_1_out, S1, not_3_out, A);
  and and_2 (and_2_out, not_1_out, not_2_out, S0, B);
  and and_3 (and_3_out, S2, not_2_out, not_3_out, C);
  or or_1 (out_7, and_1_out, and_2_out, and_3_out);
endmodule

// MUX
module mux (
  input  [4:0] A,
  input  [4:0] B,
  input  in_3,
  input  S2,
  input  S1,
  input  S0,
  output out_7,
  output out_8,
  output out_9,
  output out_10,
  output out_11
);

  mux1x1 mux1x1_1 (.S2(S2), .S1(S1), .S0(S0), .A(A[4]), .B(B[4]), .C(in_3), .out_7(out_7));
  mux1x1 mux1x1_2 (.S2(S2), .S1(S1), .S0(S0), .A(A[3]), .B(B[3]), .C(in_3), .out_7(out_8));
  mux1x1 mux1x1_3 (.S2(S2), .S1(S1), .S0(S0), .A(A[2]), .B(B[2]), .C(in_3), .out_7(out_9));
  mux1x1 mux1x1_4 (.S2(S2), .S1(S1), .S0(S0), .A(A[1]), .B(B[1]), .C(in_3), .out_7(out_10));
  mux1x1 mux1x1_5 (.S2(S2), .S1(S1), .S0(S0), .A(A[0]), .B(B[0]), .C(in_3), .out_7(out_11));
endmodule

module testes (
  input  [4:0] B,
  input  [4:0] A,
  output G,
  output F,
  output out_5,
  output E,
  output D,
  output C,
  output out_9,
  output B_2,
  output A_2,
  output out_12,
  output H,
  output out_14,
  output out_15,
  output out_16,
  output out_17,
  output out_18
);

  wire _0_out, _1_out, _2_out, _3_out, A_prime_C_out, A_prime_C_prime_out, AC_prime_out, and_1_out,
       and_2_out, and_3_out, and_4_out, and_5_out, and_6_out, and_7_out, and_8_out, and_10_out, and_11_out,
       and_12_out, and_13_out, and_14_out, and_15_out, and_16_out, and_17_out, and_18_out, and_19_out,
       and_20_out, and_21_out, and_22_out, and_23_out, and_25_out, BC_out, BD_out, C_D_out, nor_1_out,
       nor_2_out, not_1_out, not_2_out, not_3_out, not_4_out, or_1_out, or_2_out, or_3_out, or_5_out,
       or_6_out, or_7_out, or_8_out, or_9_out, or_10_out, or_11_out, or_12_out, or_13_out, or_15_out,
       or_16_out, or_17_out, or_20_out, S_out, xor_1_out, xor_2_out;

  mux1x1 mux1x1_1 (.S2(out_16), .S1(out_17), .S0(out_18), .A(A[4]), .B(B[4]), .C(1'b1), .out_7(out_5));
  mux1x1 mux1x1_2 (.S2(out_16), .S1(out_17), .S0(out_18), .A(A[3]), .B(B[3]), .C(1'b1), .out_7(out_9));
  mux1x1 mux1x1_3 (.S2(out_16), .S1(out_17), .S0(out_18), .A(A[2]), .B(B[2]), .C(1'b1), .out_7(out_12));
  mux1x1 mux1x1_4 (.S2(out_16), .S1(out_17), .S0(out_18), .A(A[1]), .B(B[1]), .C(1'b1), .out_7(out_14));
  mux1x1 mux1x1_5 (.S2(out_16), .S1(out_17), .S0(out_18), .A(A[0]), .B(B[0]), .C(1'b1), .out_7(out_15));
  and and_1 (and_1_out, A[4], B[4]);
  xor S (S_out, A[4], B[4]);
  xor _3 (_3_out, A[3], B[3]);
  xor _2 (_2_out, A[2], B[2]);
  xor _1 (_1_out, A[1], B[1]);
  xor _0 (_0_out, A[0], B[0]);
  and and_2 (and_2_out, B[4], ~A[4]);  // AND_Gate
  xor xor_1 (xor_1_out, A[4], B[4]);
  xor xor_2 (xor_2_out, and_1_out, or_3_out);
  and and_3 (and_3_out, A[3], ~B[3]);  // AND_Gate
  and and_4 (and_4_out, ~_3_out, A[2], ~B[2]);  // AND_Gate
  and and_5 (and_5_out, ~_3_out, ~_2_out, A[1], ~B[1]);  // AND_Gate
  and and_6 (and_6_out, ~_3_out, ~_2_out, ~_1_out, A[0], ~B[0]);  // AND_Gate
  nor nor_1 (nor_1_out, S_out, _3_out, _2_out, _1_out, _0_out);
  or or_1 (or_1_out, A[3], A[2], A[1], A[0]);
  or or_2 (or_2_out, B[3], B[2], B[1], B[0]);
  and and_7 (and_7_out, and_2_out, xor_1_out);
  or or_3 (or_3_out, and_3_out, and_4_out, and_5_out, and_6_out);
  or or_4 (out_16, nor_1_out, nor_2_out);
  nor nor_2 (nor_2_out, or_1_out, or_2_out);
  or or_5 (or_5_out, and_7_out, and_8_out);
  and and_8 (and_8_out, ~and_2_out, ~xor_1_out, xor_2_out);  // AND_Gate
  xnor xnor_1 (out_18, out_16, out_17);
  and and_9 (out_17, ~nor_2_out, or_5_out);  // AND_Gate
  not not_1 (not_1_out, out_9);
  not not_2 (not_2_out, out_12);
  not not_3 (not_3_out, out_14);
  not not_4 (not_4_out, out_15);
  and BC (BC_out, out_12, out_14);
  and A_prime_C_prime (A_prime_C_prime_out, not_1_out, not_3_out);
  or C_D (C_D_out, not_3_out, not_4_out);
  and A_prime_C (A_prime_C_out, not_1_out, out_14);
  and AC_prime (AC_prime_out, out_9, not_3_out);
  and BD (BD_out, out_12, out_15);
  and and_10 (and_10_out, not_2_out, not_3_out);
  or or_6 (or_6_out, out_9, out_12);
  and and_11 (and_11_out, not_3_out, not_4_out);
  and and_12 (and_12_out, not_1_out, out_14, out_15);
  or or_7 (or_7_out, and_10_out, BC_out);
  and and_13 (and_13_out, out_14, or_6_out);
  or or_8 (or_8_out, not_2_out, not_4_out);
  and and_14 (and_14_out, C_D_out, out_9);
  or or_9 (or_9_out, not_2_out, and_12_out);
  and and_15 (and_15_out, not_2_out, not_4_out);
  and and_16 (and_16_out, out_9, or_7_out);
  or or_10 (or_10_out, and_13_out, A_prime_C_prime_out);
  and and_17 (and_17_out, not_1_out, out_12, not_3_out);
  or or_11 (or_11_out, out_9, not_3_out);
  or or_12 (or_12_out, not_2_out, AC_prime_out);
  and and_18 (and_18_out, out_9, not_2_out);
  or or_13 (or_13_out, and_14_out, and_11_out);
  or or_14 (A_2, A_prime_C_out, AC_prime_out, BD_out, and_15_out);
  or or_15 (or_15_out, out_12, out_14);
  and and_19 (and_19_out, out_14, not_2_out, not_1_out);
  or or_16 (or_16_out, out_9, C_D_out);
  and and_20 (and_20_out, not_4_out, or_10_out);
  or or_17 (or_17_out, not_2_out, AC_prime_out, A_prime_C_out);
  and and_21 (and_21_out, or_11_out, BD_out);
  and and_22 (and_22_out, or_8_out, A_prime_C_out);
  and and_23 (and_23_out, not_4_out, or_12_out);
  or or_18 (C, out_15, and_18_out, BC_out, A_prime_C_prime_out);
  or or_19 (B_2, or_13_out, or_9_out);
  and and_24 (H, out_9, or_15_out);
  or or_20 (or_20_out, AC_prime_out, and_19_out);
  and and_25 (and_25_out, out_12, or_16_out);
  or or_21 (F, and_16_out, and_20_out, and_17_out);
  and and_26 (E, not_4_out, or_17_out);
  or or_22 (D, and_21_out, and_22_out, and_23_out);
  or u_G (G, or_20_out, and_25_out);
  _7_Segment_Display u_7_segment_display_1 (.b(H), .c(H));  // open: g, f, a, e, d, dp
  _7_Segment_Display u_7_segment_display_2 (.g(G), .f(F), .a(A_2), .b(B_2), .e(E), .d(D), .c(C));  // open: dp

  // Notes on the sheet:
  //   A
  //   C
  //   B
  //   F
  //   E
  //   D
endmodule

module soma (
  input  B,
  input  A,
  input  C,
  output Cout,
  output S
);

  wire and_1_out, and_2_out, and_3_out, xor_1_out;

  or or_1 (Cout, and_1_out, and_2_out, and_3_out);
  and and_1 (and_1_out, B, A);
  and and_2 (and_2_out, A, C);
  and and_3 (and_3_out, C, B);
  xor xor_1 (xor_1_out, B, A);
  xor xor_2 (S, xor_1_out, C);
endmodule

module somador (
  input  A,
  input  A_2,
  input  A_3,
  input  A_4,
  input  A_5,
  input  B,
  input  B_2,
  input  B_3,
  input  B_4,
  input  B_5,
  input  in_11,
  output out_12,
  output out_13,
  output out_14,
  output out_15,
  output out_16,
  output out_17,
  output out_18,
  output out_19,
  output out_20,
  output out_21,
  output out_22,
  output out_23
);

  wire c2maior_1_out_7, c2maior_1_out_8, c2maior_1_out_9, c2maior_1_out_10, c2maior_1_out_11,
       c2maior_1_out_12, c2maior_2_out_7, c2maior_2_out_8, c2maior_2_out_9, c2maior_2_out_10,
       c2maior_2_out_11, c2maior_2_out_12, soma_2_cout, soma_3_cout, soma_4_cout, soma_5_cout, soma_6_cout,
       xor_1_out;

  xor xor_1 (xor_1_out, B, in_11);
  c2maior c2maior_1 (
    .in_1(B_5), .in_2(B_4), .in_3(B_3), .in_4(B_2), .in_6(xor_1_out), .out_7(c2maior_1_out_7),
    .out_8(c2maior_1_out_8), .out_9(c2maior_1_out_9), .out_10(c2maior_1_out_10), .out_11(c2maior_1_out_11),
    .out_12(c2maior_1_out_12));  // open: in_5
  soma soma_1 (.B(c2maior_1_out_7), .A(c2maior_2_out_7), .S(out_12), .C(soma_3_cout));  // open: Cout
  soma soma_2 (.Cout(soma_2_cout), .B(c2maior_1_out_9), .A(c2maior_2_out_9), .S(out_14), .C(soma_4_cout));
  soma soma_3 (.Cout(soma_3_cout), .B(c2maior_1_out_8), .A(c2maior_2_out_8), .S(out_13), .C(soma_2_cout));
  soma soma_4 (.Cout(soma_4_cout), .B(c2maior_1_out_10), .A(c2maior_2_out_10), .S(out_15), .C(soma_5_cout));
  soma soma_5 (.Cout(soma_5_cout), .B(c2maior_1_out_11), .A(c2maior_2_out_11), .S(out_16), .C(soma_6_cout));
  c2maior c2maior_2 (
    .in_1(A_5), .in_2(A_4), .in_3(A_3), .in_4(A_2), .in_6(A), .out_7(c2maior_2_out_7),
    .out_8(c2maior_2_out_8), .out_9(c2maior_2_out_9), .out_10(c2maior_2_out_10), .out_11(c2maior_2_out_11),
    .out_12(c2maior_2_out_12));  // open: in_5
  soma soma_6 (.Cout(soma_6_cout), .B(c2maior_1_out_12), .A(c2maior_2_out_12), .S(out_17));  // open: C
  c2maior c2maior_3 (
    .in_1(out_17), .in_2(out_16), .in_3(out_15), .in_4(out_14), .in_5(out_13), .in_6(out_12), .out_7(out_18),
    .out_8(out_19), .out_9(out_20), .out_10(out_21), .out_11(out_22), .out_12(out_23));
endmodule

module c2maior (
  input  in_1,
  input  in_2,
  input  in_3,
  input  in_4,
  input  in_5,
  input  in_6,
  output out_7,
  output out_8,
  output out_9,
  output out_10,
  output out_11,
  output out_12
);

  wire soma_2_cout, soma_3_cout, soma_4_cout, soma_5_cout, xor_1_out, xor_2_out, xor_3_out, xor_4_out,
       xor_5_out;

  xor xor_1 (xor_1_out, in_1, in_6);
  xor xor_2 (xor_2_out, in_2, in_6);
  xor xor_3 (xor_3_out, in_3, in_6);
  xor xor_4 (xor_4_out, in_4, in_6);
  xor xor_5 (xor_5_out, in_5, in_6);
  soma soma_1 (.B(xor_5_out), .A(1'b0), .S(out_8), .C(soma_2_cout));  // open: Cout
  soma soma_2 (.Cout(soma_2_cout), .B(xor_4_out), .A(1'b0), .S(out_9), .C(soma_3_cout));
  soma soma_3 (.Cout(soma_3_cout), .B(xor_3_out), .A(1'b0), .S(out_10), .C(soma_4_cout));
  soma soma_4 (.Cout(soma_4_cout), .B(xor_2_out), .A(1'b0), .S(out_11), .C(soma_5_cout));
  soma soma_5 (.Cout(soma_5_cout), .B(xor_1_out), .A(1'b0), .S(out_12), .C(in_6));

  assign out_7 = in_6;
endmodule
